// Logisim project stage4.circ as structural Verilog: 4 circuits, main circuit main
module main (
);

  wire button_1_out, button_2_out, button_3_out, button_4_out, button_5_out, button_6_out, button_7_out,
       button_8_out, button_9_out, button_10_out, gamescore_1_out0, gamescore_1_out1, gamescore_1_out2,
       gamescore_1_out3, gamescore_1_out4, gamescore_1_out5, gamescore_2_out0, gamescore_2_out1,
       gamescore_2_out2, gamescore_2_out3, gamescore_2_out4, gamescore_2_out5, not_1_out, pointscore_1_out0,
       pointscore_1_out1, pointscore_1_out2, pointscore_2_out0, pointscore_2_out1, pointscore_2_out2,
       pointscoredisplay_1_outa0, pointscoredisplay_1_outa1, pointscoredisplay_1_outa2,
       pointscoredisplay_1_outa3, pointscoredisplay_1_outa4, pointscoredisplay_1_outa5,
       pointscoredisplay_1_outa6, pointscoredisplay_1_outb0, pointscoredisplay_1_outb1,
       pointscoredisplay_1_outb2, pointscoredisplay_1_outb3, pointscoredisplay_1_outb4,
       pointscoredisplay_1_outb5, pointscoredisplay_1_outb6, pointscoredisplay_2_outa0,
       pointscoredisplay_2_outa1, pointscoredisplay_2_outa2, pointscoredisplay_2_outa3,
       pointscoredisplay_2_outa4, pointscoredisplay_2_outa5, pointscoredisplay_2_outa6,
       pointscoredisplay_2_outb0, pointscoredisplay_2_outb1, pointscoredisplay_2_outb2,
       pointscoredisplay_2_outb3, pointscoredisplay_2_outb4, pointscoredisplay_2_outb5,
       pointscoredisplay_2_outb6, t_ff_1_q;

  Button button_1 (.out(button_1_out));
  Button button_2 (.out(button_2_out));
  Button button_3 (.out(button_3_out));
  Button button_4 (.out(button_4_out));
  Button button_5 (.out(button_5_out));
  Button button_6 (.out(button_6_out));
  T_Flip_Flop t_ff_1 (.T(1'b1), .clk(button_2_out), .Q(t_ff_1_q), .reset(button_1_out));  // open: Qn, preset
  LED led_1 (.in(not_1_out));
  LED led_2 (.in(gamescore_1_out0));
  LED led_3 (.in(gamescore_1_out1));
  LED led_4 (.in(gamescore_1_out2));
  LED led_5 (.in(t_ff_1_q));
  LED led_6 (.in(gamescore_2_out0));
  LED led_7 (.in(gamescore_2_out1));
  LED led_8 (.in(gamescore_2_out2));
  LED led_9 (.in(gamescore_1_out3));
  LED led_10 (.in(gamescore_1_out4));
  LED led_11 (.in(gamescore_1_out5));
  LED led_12 (.in(gamescore_2_out3));
  LED led_13 (.in(gamescore_2_out4));
  LED led_14 (.in(gamescore_2_out5));
  GameScore gamescore_1 (
    .Increment(button_3_out), .Decrement(button_4_out), .Reset(button_1_out), .Out0(gamescore_1_out0),
    .Out1(gamescore_1_out1), .Out2(gamescore_1_out2), .Out3(gamescore_1_out3), .Out4(gamescore_1_out4),
    .Out5(gamescore_1_out5));
  GameScore gamescore_2 (
    .Increment(button_5_out), .Decrement(button_6_out), .Reset(button_1_out), .Out0(gamescore_2_out0),
    .Out1(gamescore_2_out1), .Out2(gamescore_2_out2), .Out3(gamescore_2_out3), .Out4(gamescore_2_out4),
    .Out5(gamescore_2_out5));
  not not_1 (not_1_out, t_ff_1_q);
  Button button_7 (.out(button_7_out));
  Button button_8 (.out(button_8_out));
  Button button_9 (.out(button_9_out));
  Button button_10 (.out(button_10_out));
  _7_Segment_Display u_7_segment_display_1 (
    .g(pointscoredisplay_1_outa0), .f(pointscoredisplay_1_outa1), .a(pointscoredisplay_1_outa2),
    .b(pointscoredisplay_1_outa3), .e(pointscoredisplay_1_outa4), .d(pointscoredisplay_1_outa5),
    .c(pointscoredisplay_1_outa6));  // open: dp
  _7_Segment_Display u_7_segment_display_2 (
    .g(pointscoredisplay_2_outa0), .f(pointscoredisplay_2_outa1), .a(pointscoredisplay_2_outa2),
    .b(pointscoredisplay_2_outa3), .e(pointscoredisplay_2_outa4), .d(pointscoredisplay_2_outa5),
    .c(pointscoredisplay_2_outa6));  // open: dp
  _7_Segment_Display u_7_segment_display_3 (
    .g(pointscoredisplay_1_outb0), .f(pointscoredisplay_1_outb1), .a(pointscoredisplay_1_outb2),
    .b(pointscoredisplay_1_outb3), .e(pointscoredisplay_1_outb4), .d(pointscoredisplay_1_outb5),
    .c(pointscoredisplay_1_outb6));  // open: dp
  _7_Segment_Display u_7_segment_display_4 (
    .g(pointscoredisplay_2_outb0), .f(pointscoredisplay_2_outb1), .a(pointscoredisplay_2_outb2),
    .b(pointscoredisplay_2_outb3), .e(pointscoredisplay_2_outb4), .d(pointscoredisplay_2_outb5),
    .c(pointscoredisplay_2_outb6));  // open: dp
  PointScore pointscore_1 (
    .Increment(button_7_out), .Decrement(button_8_out), .Reset(button_1_out), .Out0(pointscore_1_out0),
    .Out1(pointscore_1_out1), .Out2(pointscore_1_out2));
  PointScore pointscore_2 (
    .Increment(button_9_out), .Decrement(button_10_out), .Reset(button_1_out), .Out0(pointscore_2_out0),
    .Out1(pointscore_2_out1), .Out2(pointscore_2_out2));
  PointScoreDisplay pointscoredisplay_1 (
    .In0(pointscore_1_out0), .In1(pointscore_1_out1), .In2(pointscore_1_out2),
    .OutA0(pointscoredisplay_1_outa0), .OutA1(pointscoredisplay_1_outa1), .OutA2(pointscoredisplay_1_outa2),
    .OutA3(pointscoredisplay_1_outa3), .OutA4(pointscoredisplay_1_outa4), .OutA5(pointscoredisplay_1_outa5),
    .OutA6(pointscoredisplay_1_outa6), .OutB0(pointscoredisplay_1_outb0), .OutB1(pointscoredisplay_1_outb1),
    .OutB2(pointscoredisplay_1_outb2), .OutB3(pointscoredisplay_1_outb3), .OutB4(pointscoredisplay_1_outb4),
    .OutB5(pointscoredisplay_1_outb5), .OutB6(pointscoredisplay_1_outb6));
  PointScoreDisplay pointscoredisplay_2 (
    .In0(pointscore_2_out0), .In1(pointscore_2_out1), .In2(pointscore_2_out2),
    .OutA0(pointscoredisplay_2_outa0), .OutA1(pointscoredisplay_2_outa1), .OutA2(pointscoredisplay_2_outa2),
    .OutA3(pointscoredisplay_2_outa3), .OutA4(pointscoredisplay_2_outa4), .OutA5(pointscoredisplay_2_outa5),
    .OutA6(pointscoredisplay_2_outa6), .OutB0(pointscoredisplay_2_outb0), .OutB1(pointscoredisplay_2_outb1),
    .OutB2(pointscoredisplay_2_outb2), .OutB3(pointscoredisplay_2_outb3), .OutB4(pointscoredisplay_2_outb4),
    .OutB5(pointscoredisplay_2_outb5), .OutB6(pointscoredisplay_2_outb6));

  // Notes on the sheet:
  //   Switch Server
  //   Player 1
  //   Games
  //   Player 2
  //   Games
  //   Reset
  //   Serving
  //   +
  //   -
  //   Serving
  //   +
  //   -
  //   This is the interface you must use. 
  //   Player 1 Points
  //   +
  //   -
  //   Player 2 Points
  //   +
  //   -
  //   TENNIS SCORE BOARD
  //    You can move components and add additional components as needed, but you must implement your solutiion using the components and subcircuits as shown
  //   Player 1 Point Score Display
  //   Player 2 Point Score Display
endmodule

module PointScore (
  input  Increment,
  input  Decrement,
  input  Reset,
  output Out0,
  output Out1,
  output Out2
);

  wire and_1_out, and_2_out, j_k_ff_1_q, j_k_ff_2_q, j_k_ff_3_q, or_1_out;

  J_K_Flip_Flop j_k_ff_1 (.J(1'b1), .K(1'b1), .clk(Increment), .Q(j_k_ff_1_q), .reset(or_1_out));  // open: Qn, preset
  D_Flip_Flop #(.trigger("falling")) d_ff_1 (
    .D(j_k_ff_1_q), .clk(Increment), .Q(Out0), .reset(or_1_out));  // open: Qn, preset
  J_K_Flip_Flop #(.trigger("falling")) j_k_ff_2 (
    .J(j_k_ff_1_q), .K(j_k_ff_1_q), .clk(Increment), .Q(j_k_ff_2_q), .reset(or_1_out));  // open: Qn, preset
  D_Flip_Flop #(.trigger("falling")) d_ff_2 (
    .D(j_k_ff_2_q), .clk(Increment), .Q(Out1), .reset(or_1_out));  // open: Qn, preset
  and and_1 (and_1_out, j_k_ff_1_q, j_k_ff_2_q);
  J_K_Flip_Flop #(.trigger("falling")) j_k_ff_3 (
    .J(and_1_out), .K(and_1_out), .clk(Increment), .Q(j_k_ff_3_q), .reset(or_1_out));  // open: Qn, preset
  D_Flip_Flop #(.trigger("falling")) d_ff_3 (
    .D(j_k_ff_3_q), .clk(Increment), .Q(Out2), .reset(or_1_out));  // open: Qn, preset
  and and_2 (and_2_out, j_k_ff_1_q, Out2);
  or or_1 (or_1_out, Reset, and_2_out);
endmodule

module PointScoreDisplay (
  input  In0,
  input  In1,
  input  In2,
  output OutA0,
  output OutA1,
  output OutA2,
  output OutA3,
  output OutA4,
  output OutA5,
  output OutA6,
  output OutB0,
  output OutB1,
  output OutB2,
  output OutB3,
  output OutB4,
  output OutB5,
  output OutB6
);

  wire Bit0_out, Bit1_out, Bit2_out, Bit3_out, Bit4_out, not_1_out, not_2_out, not_3_out, not_4_out,
       not_5_out, not_6_out, not_7_out, not_8_out, not_9_out, not_10_out;

  not not_1 (not_1_out, In2);
  not not_2 (not_2_out, In1);
  and Bit0 (Bit0_out, not_1_out, not_2_out, not_3_out);
  not not_3 (not_3_out, In0);
  not not_4 (not_4_out, In2);
  not not_5 (not_5_out, In1);
  and Bit1 (Bit1_out, not_4_out, not_5_out, In0);
  not not_6 (not_6_out, In2);
  and Bit2 (Bit2_out, not_6_out, In1, not_7_out);
  not not_7 (not_7_out, In0);
  not not_8 (not_8_out, In2);
  and Bit3 (Bit3_out, not_8_out, In1, In0);
  not not_9 (not_9_out, In1);
  and Bit4 (Bit4_out, In2, not_9_out, not_10_out);
  not not_10 (not_10_out, In0);
  or or_1 (OutA0, Bit2_out, Bit3_out, Bit4_out);
  or or_2 (OutA1, Bit0_out, Bit3_out, Bit4_out);
  or or_3 (OutA2, Bit0_out, Bit2_out, Bit4_out);
  or or_4 (OutA3, Bit0_out, Bit1_out, Bit2_out, Bit3_out, Bit4_out);
  or or_5 (OutA4, Bit0_out, Bit4_out);
  or or_6 (OutA5, Bit0_out, Bit2_out);
  or or_7 (OutA6, Bit0_out, Bit1_out, Bit2_out, Bit3_out, Bit4_out);
  or or_8 (OutB0, Bit1_out, Bit4_out);
  or or_9 (OutB1, Bit0_out, Bit1_out, Bit2_out, Bit3_out);
  or or_10 (OutB2, Bit0_out, Bit1_out, Bit2_out, Bit3_out);
  or or_11 (OutB3, Bit0_out, Bit2_out, Bit3_out, Bit4_out);
  or or_12 (OutB4, Bit0_out, Bit2_out, Bit3_out, Bit4_out);
  or or_13 (OutB5, Bit0_out, Bit1_out, Bit2_out, Bit3_out, Bit4_out);
  or or_14 (OutB6, Bit0_out, Bit1_out, Bit2_out, Bit3_out, Bit4_out);

  // Notes on the sheet:
  //   0: "00"
  //   1: "15"
  //   2: "30"
  //   3: "40"
  //   4: "Ad"
  //   2
  //   1
  //   0
  //   4
  //   5
  //   3
  //   6
endmodule

module GameScore (
  input  Increment,
  input  Decrement,
  input  Reset,
  output Out0,
  output Out1,
  output Out2,
  output Out3,
  output Out4,
  output Out5
);

  D_Flip_Flop #(.trigger("falling")) d_ff_1 (.D(1'b1), .clk(Increment), .Q(Out0), .reset(Reset));  // open: Qn, preset
  D_Flip_Flop #(.trigger("falling")) d_ff_2 (.D(Out0), .clk(Increment), .Q(Out1), .reset(Reset));  // open: Qn, preset
  D_Flip_Flop #(.trigger("falling")) d_ff_3 (.D(Out1), .clk(Increment), .Q(Out2), .reset(Reset));  // open: Qn, preset
  D_Flip_Flop #(.trigger("falling")) d_ff_4 (.D(Out2), .clk(Increment), .Q(Out3), .reset(Reset));  // open: Qn, preset
  D_Flip_Flop #(.trigger("falling")) d_ff_5 (.D(Out3), .clk(Increment), .Q(Out4), .reset(Reset));  // open: Qn, preset
  D_Flip_Flop #(.trigger("falling")) d_ff_6 (.D(Out4), .clk(Increment), .Q(Out5), .reset(Reset));  // open: Qn, preset
endmodule
