// Logisim project 3_Bit_Big_Endian_Clock_Counter.circ as structural Verilog: 1 circuit, main circuit main
module main (
  input  in_1,
  input  in_2
);

  wire and_1_out, and_2_out, and_3_out, clock_1_out, clock_2_out, j_k_ff_1_q, j_k_ff_3_q, j_k_ff_5_q,
       not_1_out;
  wire [2:0] d_ff_3_q, j_k_ff_6_q;

  and and_1 (and_1_out, j_k_ff_3_q, j_k_ff_1_q);
  J_K_Flip_Flop j_k_ff_1 (
    .J(and_2_out), .K(and_2_out), .clk(clock_1_out), .Q(j_k_ff_1_q), .reset(and_1_out));  // open: Qn, preset
  J_K_Flip_Flop j_k_ff_2 (
    .J(and_3_out), .K(and_3_out), .clk(clock_2_out), .Q(j_k_ff_6_q[2]));  // open: Qn, preset, reset
  LED led_1 (.in(j_k_ff_1_q));
  LED led_2 (.in(j_k_ff_6_q[2]));
  D_Flip_Flop d_ff_1 (.D(j_k_ff_1_q), .clk(not_1_out), .Q(d_ff_3_q[2]));  // open: Qn, preset, reset
  and and_2 (and_2_out, j_k_ff_5_q, j_k_ff_3_q);
  not not_1 (not_1_out, clock_1_out);
  J_K_Flip_Flop j_k_ff_3 (
    .J(j_k_ff_5_q), .K(j_k_ff_5_q), .clk(clock_1_out), .Q(j_k_ff_3_q), .reset(and_1_out));  // open: Qn, preset
  and and_3 (and_3_out, j_k_ff_6_q[0], j_k_ff_6_q[1]);
  J_K_Flip_Flop j_k_ff_4 (
    .J(j_k_ff_6_q[0]), .K(j_k_ff_6_q[0]), .clk(clock_2_out), .Q(j_k_ff_6_q[1]));  // open: Qn, preset, reset
  D_Flip_Flop d_ff_2 (.D(j_k_ff_3_q), .clk(not_1_out), .Q(d_ff_3_q[1]));  // open: Qn, preset, reset
  LED led_3 (.in(j_k_ff_3_q));
  J_K_Flip_Flop j_k_ff_5 (
    .J(1'b1), .K(1'b1), .clk(clock_1_out), .Q(j_k_ff_5_q), .reset(and_1_out));  // open: Qn, preset
  LED led_4 (.in(j_k_ff_6_q[1]));
  J_K_Flip_Flop j_k_ff_6 (.J(1'b1), .K(1'b1), .clk(clock_2_out), .Q(j_k_ff_6_q[0]));  // open: Qn, preset, reset
  LED led_5 (.in(j_k_ff_5_q));
  Clock clock_1 (.out(clock_1_out));
  LED led_6 (.in(j_k_ff_6_q[0]));
  Clock clock_2 (.out(clock_2_out));
  D_Flip_Flop d_ff_3 (.D(j_k_ff_5_q), .clk(not_1_out), .Q(d_ff_3_q[0]));  // open: Qn, preset, reset
  Hex_Digit_Display hex_digit_display_1 (.value({in_1, d_ff_3_q}));  // open: dp
  Hex_Digit_Display hex_digit_display_2 (.value({in_2, j_k_ff_6_q}));  // open: dp
endmodule
