// Logisim project 4_Bit_Multiplexer.circ as structural Verilog: 1 circuit, main circuit main
module main (
  input  A,
  input  B,
  input  Data0,
  input  Data1,
  input  Data2,
  input  Data3
);

  wire AND0_out, AND1_out, AND2_out, AND4_out, and_1_out, and_2_out, and_3_out, and_4_out, not_1_out,
       not_2_out, not_3_out, not_4_out, or_1_out;

  not not_1 (not_1_out, B);
  not not_2 (not_2_out, A);
  not not_3 (not_3_out, A);
  not not_4 (not_4_out, B);
  and and_1 (and_1_out, Data0, AND0_out);
  and AND0 (AND0_out, not_1_out, not_2_out);
  and and_2 (and_2_out, Data1, AND1_out);
  and AND1 (AND1_out, B, not_3_out);
  and and_3 (and_3_out, Data2, AND2_out);
  and AND2 (AND2_out, not_4_out, A);
  and and_4 (and_4_out, Data3, AND4_out);
  and AND4 (AND4_out, B, A);
  or or_1 (or_1_out, and_1_out, and_2_out, and_3_out, and_4_out);
  LED led_1 (.in(or_1_out));
endmodule
