// Logisim project 4_Bit_Register.circ as structural Verilog: 1 circuit, main circuit main
module main (
  input  PIN4,
  input  PIN3,
  input  PIN2,
  input  PIN1,
  input  RESET
);

  wire clock_1_out, d_ff_1_q, d_ff_2_q, d_ff_3_q, d_ff_4_q;

  Clock clock_1 (.out(clock_1_out));
  D_Flip_Flop d_ff_1 (.D(PIN4), .clk(clock_1_out), .Q(d_ff_1_q), .reset(RESET));  // open: Qn, preset
  LED led_1 (.in(d_ff_1_q));
  D_Flip_Flop d_ff_2 (.D(PIN3), .clk(clock_1_out), .Q(d_ff_2_q), .reset(RESET));  // open: Qn, preset
  D_Flip_Flop d_ff_3 (.D(PIN2), .clk(clock_1_out), .Q(d_ff_3_q), .reset(RESET));  // open: Qn, preset
  LED led_2 (.in(d_ff_2_q));
  D_Flip_Flop d_ff_4 (.D(PIN1), .clk(clock_1_out), .Q(d_ff_4_q), .reset(RESET));  // open: Qn, preset
  LED led_3 (.in(d_ff_3_q));
  LED led_4 (.in(d_ff_4_q));
endmodule
