// Logisim project 5_Bit_1_Wide_Stack.circ as structural Verilog: 1 circuit, main circuit main
module main (
  input  Pin11,
  input  LR2,
  input  Pin12,
  input  Pin22,
  input  Reset2,
  input  LR3,
  input  Pin13,
  input  Reset3,
  input  Dump1,
  input  DumpReset1
);

  wire and_1_out, and_2_out, and_3_out, and_4_out, and_5_out, and_6_out, and_7_out, and_8_out, and_9_out,
       and_10_out, and_11_out, and_12_out, and_13_out, and_14_out, Clock1_out, Clock2_out, Clock3_out,
       d_ff_1_q, d_ff_2_q, d_ff_3_q, d_ff_4_q, d_ff_5_q, d_ff_6_q, d_ff_7_q, d_ff_8_q, d_ff_9_q, d_ff_10_q,
       d_ff_11_q, d_ff_12_q, d_ff_13_q, d_ff_14_q, d_ff_15_q, not_1_out, not_2_out, or_1_out, or_2_out,
       or_3_out, or_4_out, or_5_out, or_6_out, or_7_out;

  D_Flip_Flop d_ff_1 (.D(Pin11), .clk(Clock1_out), .Q(d_ff_1_q));  // open: Qn, preset, reset
  Clock Clock1 (.out(Clock1_out));
  Clock Clock3 (.out(Clock3_out));
  D_Flip_Flop d_ff_2 (.D(d_ff_1_q), .clk(Clock1_out), .Q(d_ff_2_q));  // open: Qn, preset, reset
  LED led_1 (.in(d_ff_1_q));
  not not_1 (not_1_out, LR3);
  and and_1 (and_1_out, LR3, Pin13);
  and and_2 (and_2_out, not_1_out, d_ff_6_q);
  or or_1 (or_1_out, and_1_out, and_2_out);
  D_Flip_Flop d_ff_3 (.D(or_1_out), .clk(Clock3_out), .Q(d_ff_3_q), .reset(Reset3));  // open: Qn, preset
  D_Flip_Flop d_ff_4 (.D(d_ff_2_q), .clk(Clock1_out), .Q(d_ff_4_q));  // open: Qn, preset, reset
  LED led_2 (.in(d_ff_2_q));
  D_Flip_Flop d_ff_5 (.D(d_ff_3_q), .clk(Dump1), .Q(d_ff_5_q), .reset(DumpReset1));  // open: Qn, preset
  LED led_3 (.in(d_ff_3_q));
  LED led_4 (.in(d_ff_4_q));
  and and_3 (and_3_out, LR3, d_ff_3_q);
  and and_4 (and_4_out, not_1_out, d_ff_8_q);
  or or_2 (or_2_out, and_3_out, and_4_out);
  D_Flip_Flop d_ff_6 (.D(or_2_out), .clk(Clock3_out), .Q(d_ff_6_q), .reset(Reset3));  // open: Qn, preset
  LED led_5 (.in(d_ff_5_q));
  and and_5 (and_5_out, LR3, d_ff_6_q);
  D_Flip_Flop d_ff_7 (.D(d_ff_6_q), .clk(Dump1), .Q(d_ff_7_q), .reset(DumpReset1));  // open: Qn, preset
  LED led_6 (.in(d_ff_6_q));
  not not_2 (not_2_out, LR2);
  and and_6 (and_6_out, LR2, Pin12);
  Clock Clock2 (.out(Clock2_out));
  and and_7 (and_7_out, not_1_out, d_ff_11_q);
  or or_3 (or_3_out, and_5_out, and_7_out);
  D_Flip_Flop d_ff_8 (.D(or_3_out), .clk(Clock3_out), .Q(d_ff_8_q), .reset(Reset3));  // open: Qn, preset
  LED led_7 (.in(d_ff_8_q));
  LED led_8 (.in(d_ff_7_q));
  and and_8 (and_8_out, not_2_out, d_ff_12_q);
  or or_4 (or_4_out, and_6_out, and_8_out);
  D_Flip_Flop d_ff_9 (.D(or_4_out), .clk(Clock2_out), .Q(d_ff_9_q), .reset(Reset2));  // open: Qn, preset
  and and_9 (and_9_out, LR3, d_ff_8_q);
  or or_5 (or_5_out, and_9_out, and_11_out);
  D_Flip_Flop d_ff_10 (.D(d_ff_8_q), .clk(Dump1), .Q(d_ff_10_q), .reset(DumpReset1));  // open: Qn, preset
  and and_10 (and_10_out, LR2, d_ff_9_q);
  or or_6 (or_6_out, and_10_out, and_12_out);
  LED led_9 (.in(d_ff_9_q));
  and and_11 (and_11_out, not_1_out, d_ff_13_q);
  D_Flip_Flop d_ff_11 (.D(or_5_out), .clk(Clock3_out), .Q(d_ff_11_q), .reset(Reset3));  // open: Qn, preset
  LED led_10 (.in(d_ff_11_q));
  LED led_11 (.in(d_ff_10_q));
  and and_12 (and_12_out, not_2_out, Pin22);
  D_Flip_Flop d_ff_12 (.D(or_6_out), .clk(Clock2_out), .Q(d_ff_12_q), .reset(Reset2));  // open: Qn, preset
  LED led_12 (.in(d_ff_12_q));
  and and_13 (and_13_out, LR3, d_ff_11_q);
  and and_14 (and_14_out, not_1_out, Pin13);
  or or_7 (or_7_out, and_13_out, and_14_out);
  D_Flip_Flop d_ff_13 (.D(or_7_out), .clk(Clock3_out), .Q(d_ff_13_q), .reset(Reset3));  // open: Qn, preset
  D_Flip_Flop d_ff_14 (.D(d_ff_11_q), .clk(Dump1), .Q(d_ff_14_q), .reset(DumpReset1));  // open: Qn, preset
  LED led_13 (.in(d_ff_14_q));
  D_Flip_Flop d_ff_15 (.D(d_ff_13_q), .clk(Dump1), .Q(d_ff_15_q), .reset(DumpReset1));  // open: Qn, preset
  LED led_14 (.in(d_ff_13_q));
  LED led_15 (.in(d_ff_15_q));
endmodule
