// Logisim project 8_Bit_Multiplexer.circ as structural Verilog: 1 circuit, main circuit main
module main (
  input  N4,
  input  N2,
  input  N1,
  input  DATA0,
  input  DATA1,
  input  DATA2,
  input  DATA3,
  input  DATA4,
  input  DATA5,
  input  DATA6,
  input  DATA7
);

  wire AND0_out, AND1_out, AND2_out, AND3_out, AND4_out, AND5_out, AND6_out, AND7_out, and_1_out, and_2_out,
       and_3_out, and_4_out, and_5_out, and_6_out, and_7_out, and_8_out, not_1_out, not_2_out, not_3_out,
       not_4_out, not_5_out, not_6_out, not_7_out, not_8_out, not_9_out, not_10_out, not_11_out, not_12_out,
       or_1_out;

  not not_1 (not_1_out, N1);
  not not_2 (not_2_out, N2);
  and AND0 (AND0_out, not_1_out, not_2_out, not_3_out);
  not not_3 (not_3_out, N4);
  not not_4 (not_4_out, N2);
  and AND1 (AND1_out, N1, not_4_out, not_5_out);
  not not_5 (not_5_out, N4);
  not not_6 (not_6_out, N1);
  and AND2 (AND2_out, not_6_out, N2, not_7_out);
  not not_7 (not_7_out, N4);
  and AND3 (AND3_out, N1, N2, not_8_out);
  not not_8 (not_8_out, N4);
  not not_9 (not_9_out, N1);
  not not_10 (not_10_out, N2);
  and AND4 (AND4_out, not_9_out, not_10_out, N4);
  not not_11 (not_11_out, N2);
  and AND5 (AND5_out, N1, not_11_out, N4);
  not not_12 (not_12_out, N1);
  and AND6 (AND6_out, not_12_out, N2, N4);
  and AND7 (AND7_out, N1, N2, N4);
  and and_1 (and_1_out, DATA0, AND0_out);
  and and_2 (and_2_out, DATA1, AND1_out);
  and and_3 (and_3_out, DATA2, AND2_out);
  and and_4 (and_4_out, DATA3, AND3_out);
  and and_5 (and_5_out, DATA4, AND4_out);
  and and_6 (and_6_out, DATA5, AND5_out);
  and and_7 (and_7_out, DATA6, AND6_out);
  and and_8 (and_8_out, DATA7, AND7_out);
  or or_1 (or_1_out, and_1_out, and_2_out, and_3_out, and_4_out, and_5_out, and_6_out, and_7_out, and_8_out);
  LED led_1 (.in(or_1_out));
endmodule
