// Logisim project 8_Bit_Multiplexer_and_Demultiplexer.circ as structural Verilog: 1 circuit, main circuit main
module main (
  input  N4,
  input  N2,
  input  N1,
  input  B4,
  input  B2,
  input  B1,
  input  DATA0,
  input  DATA1,
  input  DATA2,
  input  DATA3,
  input  DATA4,
  input  DATA5,
  input  DATA6,
  input  DATA7
);

  wire AND0_out, AND1_out, AND2_out, AND3_out, AND4_out, AND5_out, AND6_out, AND7_out, and_1_out, and_2_out,
       and_3_out, and_4_out, and_5_out, and_6_out, and_7_out, and_8_out, not_1_out, not_2_out, not_3_out,
       not_4_out, not_5_out, not_6_out, not_7_out, not_8_out, not_9_out, not_10_out, not_11_out, not_12_out,
       not_13_out, not_14_out, not_15_out, or_1_out, or_2_out, OUT0_out, OUT1_out, OUT2_out, OUT3_out,
       OUT4_out, OUT5_out, OUT6_out, OUT7_out;

  not not_1 (not_1_out, N1);
  not not_2 (not_2_out, N2);
  and AND0 (AND0_out, not_1_out, not_2_out, not_3_out);
  not not_3 (not_3_out, N4);
  not not_4 (not_4_out, N2);
  and AND1 (AND1_out, N1, not_4_out, not_5_out);
  not not_5 (not_5_out, N4);
  not not_6 (not_6_out, N1);
  and AND2 (AND2_out, not_6_out, N2, not_7_out);
  not not_7 (not_7_out, N4);
  and AND3 (AND3_out, N1, N2, not_8_out);
  not not_8 (not_8_out, N4);
  not not_9 (not_9_out, N1);
  not not_10 (not_10_out, N2);
  and AND4 (AND4_out, not_9_out, not_10_out, N4);
  not not_11 (not_11_out, N2);
  and AND5 (AND5_out, N1, not_11_out, N4);
  not not_12 (not_12_out, N1);
  and AND6 (AND6_out, not_12_out, N2, N4);
  and AND7 (AND7_out, N1, N2, N4);
  and and_1 (and_1_out, DATA0, AND0_out);
  and and_2 (and_2_out, DATA1, AND1_out);
  and and_3 (and_3_out, DATA2, AND2_out);
  and and_4 (and_4_out, DATA3, AND3_out);
  and and_5 (and_5_out, DATA4, AND4_out);
  and and_6 (and_6_out, DATA5, AND5_out);
  and and_7 (and_7_out, DATA6, AND6_out);
  and and_8 (and_8_out, DATA7, AND7_out);
  or or_1 (or_1_out, and_1_out, and_2_out, and_3_out, and_4_out, and_5_out, and_6_out, and_7_out, and_8_out);
  not not_13 (not_13_out, B4);
  not not_14 (not_14_out, B2);
  not not_15 (not_15_out, B1);
  and OUT0 (OUT0_out, not_15_out, not_14_out, not_13_out, or_1_out);
  and OUT1 (OUT1_out, B1, not_14_out, not_13_out, or_1_out);
  and OUT2 (OUT2_out, not_15_out, B2, not_13_out, or_1_out);
  and OUT3 (OUT3_out, B1, B2, not_13_out, or_1_out);
  and OUT4 (OUT4_out, not_15_out, not_14_out, B4, or_1_out);
  and OUT5 (OUT5_out, B1, not_14_out, B4, or_1_out);
  and OUT6 (OUT6_out, not_15_out, B2, B4, or_1_out);
  and OUT7 (OUT7_out, B1, B2, B4, or_1_out);
  or or_2 (or_2_out, OUT0_out, OUT1_out, OUT2_out, OUT3_out, OUT4_out, OUT5_out, OUT6_out, OUT7_out);
  LED led_1 (.in(or_2_out));
endmodule
