// Logisim project JK_Flip_Flop.circ as structural Verilog: 1 circuit, main circuit main
module main (
  input  J,
  input  K
);

  wire and_1_out, and_2_out, clock_1_out, nand_1_out, nand_2_out;

  Clock clock_1 (.out(clock_1_out));
  and and_1 (and_1_out, nand_2_out, J, clock_1_out);
  and and_2 (and_2_out, clock_1_out, K, nand_1_out);
  nand nand_1 (nand_1_out, and_1_out, nand_2_out);
  nand nand_2 (nand_2_out, nand_1_out, and_2_out);
  LED Q (.in(nand_1_out));
  LED QQ (.in(nand_2_out));
endmodule
