// Logisim project RS_Flip_Flop.circ as structural Verilog: 1 circuit, main circuit main
module main (
  input  in_1,
  input  in_2
);

  wire nor_1_out, nor_2_out;

  nor nor_1 (nor_1_out, in_1, nor_2_out);
  LED led_1 (.in(nor_1_out));
  nor nor_2 (nor_2_out, nor_1_out, in_2);
  LED led_2 (.in(nor_2_out));
endmodule
