// Logisim project XNOR_Gate.circ as structural Verilog: 1 circuit, main circuit main
module main (
  input  in_1,
  input  in_2,
  input  in_3,
  input  in_4
);

  wire not_1_out, xnor_1_out, xor_1_out;

  xor xor_1 (xor_1_out, in_1, in_2);
  xnor xnor_1 (xnor_1_out, in_3, in_4);
  not not_1 (not_1_out, xor_1_out);
  LED led_1 (.in(not_1_out));
  LED led_2 (.in(xnor_1_out));
endmodule
