// Logisim project XOR_Gate.circ as structural Verilog: 1 circuit, main circuit main
module main (
  input  in_1,
  input  in_2
);

  wire xor_1_out;

  xor xor_1 (xor_1_out, in_1, in_2);
  LED led_1 (.in(xor_1_out));
endmodule
